# Fritzing sketch uglimes (saved by Fritzing 0.9.9b)
breadboards: 1

parts:
  Part1 = Arduino Uno (Rev3)
  LED1 = smd LED [color="Red (660nm)" part_number=U package="0603 [SMD]"]
  LED3 = smd LED [color="White (4500K)" part_number=- package="0603 [SMD]"]
  LED4 = smd LED [color="Blue (525nm)" part_number=L package="0603 [SMD]"]
  LED2 = smd LED [color="Green (570nm)" part_number=G package="0603 [SMD]"]
  R1 = Resistor [tolerance=±5% power=0pW resistance=1k package=THT]
  R2 = Resistor [tolerance=±5% power=0pW resistance=100 package=THT]
  R3 = Resistor [tolerance=±5% power=0pW resistance=4.7k package=THT]
  LED5 = smd LED [color="Red (660nm)" part_number=I package="0603 [SMD]"]
  LED6 = smd LED [color="Green (570nm)" part_number=M package="0603 [SMD]"]
  LED7 = smd LED [color="Blue (525nm)" part_number=E package="0603 [SMD]"]
  LED8 = smd LED [color="Red (660nm)" part_number=S package="0603 [SMD]"]
  R4 = Resistor [tolerance=±5% power=0pW resistance=4.7k package=THT]
  R5 = Resistor [tolerance=±5% power=0pW resistance=1k package=THT]
  R6 = Resistor [tolerance=±5% power=0pW resistance=100 package=THT]
  R7 = Resistor [tolerance=±5% power=0pW resistance=4.7k package=THT]
  R8 = Resistor [tolerance=±5% power=0pW resistance=1k package=THT]

nets:
  N1: Part1.D8, R7.Pin_0
  N2: Part1.D9_PWM, R8.Pin_0
  N3: Part1.D10_PWM/SS, LED1.cathode, LED3.cathode, LED4.cathode, LED2.cathode, LED5.cathode, LED6.cathode, LED7.cathode, LED8.cathode
  N4: Part1.D2, R1.Pin_0
  N5: Part1.D3_PWM, R2.Pin_0
  N6: Part1.D4, R3.Pin_0
  N7: Part1.D5_PWM, R4.Pin_0
  N8: Part1.D6_PWM, R5.Pin_0
  N9: Part1.D7, R6.Pin_0
  N10: LED1.anode, R1.Pin_1
  N11: LED3.anode, R3.Pin_1
  N12: LED4.anode, R4.Pin_1
  N13: LED2.anode, R2.Pin_1
  N14: LED5.anode, R5.Pin_1
  N15: LED6.anode, R6.Pin_1
  N16: LED7.anode, R7.Pin_1
  N17: LED8.anode, R8.Pin_1
